// Logisim project 9进制加法器.circ as structural Verilog: 1 circuit, main circuit main
module main (
);

  wire and_1_out, and_2_out, and_3_out, and_4_out, and_5_out, button_1_out, button_3_out, d_ff_1_qn,
       d_ff_2_q, d_ff_2_qn, d_ff_3_q, d_ff_3_qn, d_ff_4_q, d_ff_4_qn, digital_oscilloscope_1_p2,
       digital_oscilloscope_1_p3, or_1_out, xor_1_out;

  Button button_1 (.out(button_1_out));
  // Digital_Oscilloscope #(.nState(10), .frontlines("rising"), .showclock("true")) digital_oscilloscope_1: pin names not known; wires that end beside it: button_1_out, digital_oscilloscope_1_p2, digital_oscilloscope_1_p3
  Button button_2 (.out(digital_oscilloscope_1_p3));
  D_Flip_Flop #(.trigger("rising"), .Pre_Clr_Positions("ABOVE_BELOW"), .NegatePresetClear("false"), .enable("false"), .NewFFLayout("true")) d_ff_1 (
    .clk(button_1_out), .D(and_3_out), .Q(digital_oscilloscope_1_p2), .Qn(d_ff_1_qn), .reset(button_3_out));  // open: preset
  Button button_3 (.out(button_3_out));
  LED #(.active("true")) led_1 (.in(digital_oscilloscope_1_p2));
  D_Flip_Flop #(.trigger("rising"), .Pre_Clr_Positions("ABOVE_BELOW"), .NegatePresetClear("false"), .enable("false"), .NewFFLayout("true")) d_ff_2 (
    .clk(button_1_out), .D(or_1_out), .Q(d_ff_2_q), .Qn(d_ff_2_qn));  // open: preset, reset
  and and_1 (and_1_out, d_ff_2_q, d_ff_3_qn);
  LED #(.active("true")) led_2 (.in(d_ff_2_q));
  and and_2 (and_2_out, d_ff_2_q, d_ff_4_qn);
  D_Flip_Flop #(.trigger("rising"), .Pre_Clr_Positions("ABOVE_BELOW"), .NegatePresetClear("false"), .enable("false"), .NewFFLayout("true")) d_ff_3 (
    .clk(button_1_out), .D(xor_1_out), .Q(d_ff_3_q), .Qn(d_ff_3_qn));  // open: preset, reset
  and and_3 (and_3_out, d_ff_2_q, d_ff_3_q, d_ff_4_q);
  or or_1 (or_1_out, and_1_out, and_2_out, and_4_out);
  LED #(.active("true")) led_3 (.in(d_ff_3_q));
  and and_4 (and_4_out, d_ff_2_qn, d_ff_3_q, d_ff_4_q);
  xor xor_1 (xor_1_out, d_ff_3_q, d_ff_4_q);
  and and_5 (and_5_out, d_ff_1_qn, d_ff_4_qn);
  D_Flip_Flop #(.trigger("rising"), .Pre_Clr_Positions("ABOVE_BELOW"), .NegatePresetClear("false"), .enable("false"), .NewFFLayout("true")) d_ff_4 (
    .clk(button_1_out), .D(and_5_out), .Q(d_ff_4_q), .Qn(d_ff_4_qn));  // open: preset, reset
  LED #(.active("true")) led_4 (.in(d_ff_4_qn));
endmodule
