// Logisim project 半加器.circ as structural Verilog: 1 circuit, main circuit main
module main (
  input  A,
  input  B,
  input  A_2,
  input  B_2,
  input  cin,
  input  A1,
  input  B1,
  input  A0,
  input  B0,
  input  A2,
  input  B2,
  input  A3,
  input  B3,
  output cout,
  output sum,
  output sum_2,
  output cout_2,
  output Sum1,
  output Sum2,
  output Sum0,
  output Sum3,
  output Cout_3
);

  wire and_2_out, and_3_out, and_4_out, and_5_out, and_6_out, nand_1_out, nand_2_out, nand_4_out, nand_5_out,
       nand_6_out, nand_7_out, nand_8_out, nand_9_out, nand_10_out, nand_11_out, not_1_out, not_2_out,
       not_3_out, not_4_out, xor_1_out, xor_3_out, xor_5_out, xor_7_out;

  not not_1 (not_1_out, A);
  not not_2 (not_2_out, B);
  xor xor_1 (xor_1_out, A_2, B_2);
  nand nand_1 (nand_1_out, A_2, B_2);
  and and_1 (cout, A, B);
  and and_2 (and_2_out, B, not_1_out);
  and and_3 (and_3_out, A, not_2_out);
  not not_3 (not_3_out, A0);
  not not_4 (not_4_out, B0);
  or or_1 (sum, and_2_out, and_3_out);
  xor xor_2 (sum_2, xor_1_out, cin);
  nand nand_2 (nand_2_out, cin, xor_1_out);
  nand nand_3 (cout_2, nand_2_out, nand_1_out);
  and and_4 (and_4_out, A0, B0);
  and and_5 (and_5_out, B0, not_3_out);
  and and_6 (and_6_out, A0, not_4_out);
  or or_2 (Sum0, and_5_out, and_6_out);
  xor xor_3 (xor_3_out, A1, B1);
  nand nand_4 (nand_4_out, A1, B1);
  xor xor_4 (Sum1, xor_3_out, and_4_out);
  nand nand_5 (nand_5_out, and_4_out, xor_3_out);
  nand nand_6 (nand_6_out, nand_5_out, nand_4_out);
  xor xor_5 (xor_5_out, A2, B2);
  nand nand_7 (nand_7_out, A2, B2);
  xor xor_6 (Sum2, xor_5_out, nand_6_out);
  nand nand_8 (nand_8_out, nand_6_out, xor_5_out);
  nand nand_9 (nand_9_out, nand_8_out, nand_7_out);
  xor xor_7 (xor_7_out, A3, B3);
  nand nand_10 (nand_10_out, A3, B3);
  xor xor_8 (Sum3, xor_7_out, nand_9_out);
  nand nand_11 (nand_11_out, nand_9_out, xor_7_out);
  nand nand_12 (Cout_3, nand_11_out, nand_10_out);
endmodule
