// Logisim project 序列发生器01000101.circ as structural Verilog: 2 circuits, main circuit main
module main (
  input  in_1,
  input  in_2,
  input  in_3
);

  wire and_1_out, and_2_out, and_3_out, button_1_out, button_2_out, button_3_out, button_4_out, button_5_out,
       D1_qn, D2_qn, D3_qn, decoder_1_out1, decoder_1_out5, decoder_1_out7, digital_oscilloscope_1_p3,
       digital_oscilloscope_2_p3, digital_oscilloscope_3_p6, multiplexer_1_out, or_1_out, or_2_out,
       shift_register_1_out, shift_register_1_q7, xor_1_out;
  wire [2:0] counter_1_q, D1_q;

  Button button_1 (.out(button_1_out));
  Counter #(.width(3), .max('h7), .ongoal("wrap"), .trigger("rising"), .behavior("new")) counter_1 (
    .load(in_3), .Q(counter_1_q), .clk(button_1_out), .clr(button_2_out));  // open: D, count, carry, preset, down
  Button button_2 (.out(button_2_out));
  Button button_3 (.out(button_3_out));
  Button button_4 (.out(button_4_out));
  or or_1 (or_1_out, and_1_out, and_2_out, and_3_out);
  and and_1 (and_1_out, D3_qn, D1_q[1], D1_q[0]);
  and and_2 (and_2_out, D2_qn, D1_q[2]);
  and and_3 (and_3_out, D1_q[2], D1_qn);
  Shift_Register #(.width(1), .length(8), .parallel("true"), .trigger("rising")) shift_register_1 (
    .in(shift_register_1_q7), .clk(button_3_out), .out(shift_register_1_out), .clr(button_5_out),
    .q7(shift_register_1_q7));  // open: shift, load, d0, q0, d1, q1, d2, q2, d3, q3, d4, q4, d5, q5, d6, q6, d7
  Button button_5 (.out(button_5_out));
  D_Flip_Flop #(.trigger("rising"), .Pre_Clr_Positions("ABOVE_BELOW"), .NegatePresetClear("false"), .enable("false"), .NewFFLayout("true")) D3 (
    .clk(button_4_out), .D(or_1_out), .Q(D1_q[2]), .Qn(D3_qn));  // open: preset, reset
  Decoder #(.select(3), .tristate("false"), .disabled("Z"), .enable("false")) decoder_1 (
    .out1(decoder_1_out1), .out5(decoder_1_out5), .out7(decoder_1_out7), .sel(counter_1_q));  // open: out0, out2, out3, out4, out6
  // Digital_Oscilloscope #(.nState(10), .frontlines("rising"), .showclock("true")) digital_oscilloscope_1: pin names not known; wires that end beside it: button_3_out, shift_register_1_out, digital_oscilloscope_1_p3
  xor xor_1 (xor_1_out, D1_q[1], D1_q[0]);
  Button button_6 (.out(digital_oscilloscope_1_p3));
  D_Flip_Flop #(.trigger("rising"), .Pre_Clr_Positions("ABOVE_BELOW"), .NegatePresetClear("false"), .enable("false"), .NewFFLayout("true")) D2 (
    .clk(button_4_out), .D(xor_1_out), .Q(D1_q[1]), .Qn(D2_qn));  // open: preset, reset
  or or_2 (or_2_out, decoder_1_out1, decoder_1_out5, decoder_1_out7);
  // Digital_Oscilloscope #(.nState(10), .frontlines("rising"), .showclock("true")) digital_oscilloscope_2: pin names not known; wires that end beside it: button_1_out, or_2_out, digital_oscilloscope_2_p3
  Button button_7 (.out(digital_oscilloscope_2_p3));
  D_Flip_Flop #(.trigger("rising"), .Pre_Clr_Positions("ABOVE_BELOW"), .NegatePresetClear("false"), .enable("false"), .NewFFLayout("true")) D1 (
    .clk(button_4_out), .D(D1_qn), .Q(D1_q[0]), .Qn(D1_qn));  // open: preset, reset
  Multiplexer #(.select(3), .width(1), .disabled("Z"), .enable("false")) multiplexer_1 (
    .in0(in_1), .in1(in_2), .in2(in_1), .in3(in_1), .in4(in_1), .in5(in_2), .in6(in_1), .in7(in_2),
    .out(multiplexer_1_out), .sel(D1_q));
  // Digital_Oscilloscope #(.nState(10), .frontlines("rising"), .showclock("true")) digital_oscilloscope_3: pin names not known; wires that end beside it: button_4_out, D1_q[2], D1_q[1], D1_q[0], multiplexer_1_out, digital_oscilloscope_3_p6
  Button button_8 (.out(digital_oscilloscope_3_p6));

  // Notes on the sheet:
  //   输出
  //   这个是发生器
endmodule

module \序列发生器01010011  (
);

  wire [2:0] undriven;

  main main_1 (.in_1(undriven[2]), .in_2(undriven[1]), .in_3(undriven[0]));
  Multiplexer #(.select(3), .width(3), .disabled("Z"), .enable("false")) multiplexer_1 (.sel(undriven));  // open: in0, in1, in2, in3, in4, in5, in6, in7, out
endmodule
