// Logisim project 检测器.circ as structural Verilog: 1 circuit, main circuit main
module main (
  input  in_1,
  input  in_2,
  input  X
);

  wire _0_q, _0_qn, _1_q, _1_qn, _2_q, _2_qn, and_1_out, and_2_out, and_3_out, and_4_out, and_5_out,
       and_6_out, button_1_out, button_2_out, button_3_out, digital_oscilloscope_1_p6,
       digital_oscilloscope_2_p4, j_k_ff_1_q, j_k_ff_2_q, not_1_out, not_2_out, or_1_out, or_2_out, or_3_out;

  Button button_1 (.out(button_1_out));
  Button button_2 (.out(button_2_out));
  not not_1 (not_1_out, in_1);
  and and_1 (and_1_out, _1_q, _0_q, not_2_out);
  and and_2 (and_2_out, _0_qn, _2_qn, X);
  or or_1 (or_1_out, and_2_out, and_3_out);
  and and_3 (and_3_out, _0_q, _2_qn, not_2_out);
  J_K_Flip_Flop #(.trigger("rising"), .Pre_Clr_Positions("ABOVE_BELOW"), .NegatePresetClear("false"), .enable("false"), .NewFFLayout("true")) j_k_ff_1 (
    .J(and_4_out), .clk(button_1_out), .K(or_2_out), .Q(j_k_ff_1_q), .reset(button_3_out));  // open: Qn, preset
  and and_4 (and_4_out, not_1_out, j_k_ff_2_q);
  Button button_3 (.out(button_3_out));
  not not_2 (not_2_out, X);
  or or_2 (or_2_out, not_1_out, j_k_ff_2_q);
  J_K_Flip_Flop #(.trigger("rising"), .Pre_Clr_Positions("ABOVE_BELOW"), .NegatePresetClear("false"), .enable("false"), .NewFFLayout("true")) _2 (
    .J(and_1_out), .clk(button_2_out), .K(in_2), .Q(_2_q), .Qn(_2_qn));  // open: preset, reset
  or or_3 (or_3_out, _2_q, _0_q, not_2_out);
  J_K_Flip_Flop #(.trigger("rising"), .Pre_Clr_Positions("ABOVE_BELOW"), .NegatePresetClear("false"), .enable("false"), .NewFFLayout("true")) j_k_ff_2 (
    .J(in_1), .clk(button_1_out), .K(not_1_out), .Q(j_k_ff_2_q));  // open: Qn, preset, reset
  J_K_Flip_Flop #(.trigger("rising"), .Pre_Clr_Positions("ABOVE_BELOW"), .NegatePresetClear("false"), .enable("false"), .NewFFLayout("true")) _1 (
    .J(or_1_out), .clk(button_2_out), .K(or_3_out), .Q(_1_q), .Qn(_1_qn));  // open: preset, reset
  and and_5 (and_5_out, j_k_ff_2_q, not_1_out, j_k_ff_1_q);
  J_K_Flip_Flop #(.trigger("rising"), .Pre_Clr_Positions("ABOVE_BELOW"), .NegatePresetClear("false"), .enable("false"), .NewFFLayout("true")) _0 (
    .J(X), .clk(button_2_out), .K(not_2_out), .Q(_0_q), .Qn(_0_qn));  // open: preset, reset
  and and_6 (and_6_out, _0_qn, _1_qn, _2_q);
  // Digital_Oscilloscope #(.nState(10), .frontlines("rising"), .showclock("true")) digital_oscilloscope_1: pin names not known; wires that end beside it: button_1_out, in_1, j_k_ff_2_q, and_5_out, j_k_ff_1_q, digital_oscilloscope_1_p6
  Button button_4 (.out(digital_oscilloscope_1_p6));
  // Digital_Oscilloscope #(.nState(10), .frontlines("rising"), .showclock("true")) digital_oscilloscope_2: pin names not known; wires that end beside it: button_2_out, X, and_6_out, digital_oscilloscope_2_p4
  Button button_5 (.out(digital_oscilloscope_2_p4));

  // Notes on the sheet:
  //   输出
  //   这个是检测器
  //   时钟信号
  //   输入
  //   输出
endmodule
